# Fritzing sketch gas-station (saved by Fritzing 0.9.3b)
breadboards: 1

parts:
  U1 = atmega328 [package=dip]
  R1 = Resistor [tolerance=±5% resistance=150 package="0603 [SMD]"]
  SP1 = SPEAKER [package=pcb_mount_speaker]
  S1 = Round Pushbutton
  7_Segment1 = 7 Segment Display
  7_Segment2 = 7 Segment Display
  7_Segment3 = 7 Segment Display
  XTAL1 = Crystal [frequency="16 Mhz" package=THT]
  Y1 = Resonator [frequency="16 Mhz" package=THT]
  Y2 = Resonator [frequency="16 Mhz" package=THT]
  VCC1 = 4 x AAA Battery Mount

nets:
  N1: U1.D2, S1.leg1
  N2: U1.D3_(PWM), R1.Pin_1
  N3: U1.D4, 7_Segment1.common_cathode
  N4: U1.VCC, U1.AVCC, VCC1.+
  N5: U1.GND, SP1.+, S1.leg0, Y1.1, Y2.0, VCC1.-
  N6: U1.XLAT1, XTAL1.pin_0, Y2.1
  N7: U1.XLAT2, XTAL1.pin_1, Y1.0
  N8: U1.D5_(PWM), 7_Segment1.Segment_B, 7_Segment2.Segment_B, 7_Segment3.Segment_B
  N9: U1.D6_(PWM), 7_Segment1.Segment_A, 7_Segment2.Segment_A, 7_Segment3.Segment_A
  N10: U1.D7, 7_Segment1.Segment_F, 7_Segment2.Segment_F, 7_Segment3.Segment_F
  N11: U1.D8, 7_Segment1.Segment_G, 7_Segment2.Segment_G, 7_Segment3.Segment_G
  N12: U1.D9_(PWM), 7_Segment1.Segment_E, 7_Segment2.Segment_E, 7_Segment3.Segment_E
  N13: U1.D10_(PWM), 7_Segment1.Segment_D, 7_Segment2.Segment_D, 7_Segment3.Segment_D
  N14: U1.D11_(PWM), 7_Segment1.Segment_C, 7_Segment2.Segment_C, 7_Segment3.Segment_C
  N15: U1.D12, 7_Segment2.common_cathode
  N16: U1.D13, 7_Segment3.common_cathode
  N17: R1.Pin_0, SP1.-
